# Fritzing sketch LEDdimmer (saved by Fritzing 0.9.3b)
breadboards: 1

parts:
  Q1 = Basic FET N-Channel [package="TO220 [THT]"]
  Q2 = Basic FET N-Channel [package="TO220 [THT]"]
  Q3 = Basic FET N-Channel [package="TO220 [THT]"]
  Q4 = Basic FET N-Channel [package="TO220 [THT]"]
  U1 = Voltage Regulator - 5V [package="TO220 [THT]"]
  WeMos_D1_Mini1 = WeMos D1 Mini
  J1 = Camdenboss CTB0158-5 [part_number=CTB0158-5 package=THT]
  J2 = Camdenboss CTB0158-2 [part_number=CTB0158-2 package=THT]

nets:
  N1: Q1.gate, WeMos_D1_Mini1.D1
  N2: Q1.drain, J1.pin2
  N3: Q1.source, Q2.source, Q3.source, Q4.source, U1.GND, J2.pin2
  N4: Q2.gate, WeMos_D1_Mini1.D2
  N5: Q2.drain, J1.pin3
  N6: Q3.gate, WeMos_D1_Mini1.D3
  N7: Q3.drain, J1.pin4
  N8: Q4.gate, WeMos_D1_Mini1.D4
  N9: Q4.drain, J1.pin5
  N10: U1.input_voltage, J1.pin1, J2.pin1
  N11: U1.output_voltage, WeMos_D1_Mini1.5V
